# Fritzing sketch aufbau_roboter (saved by Fritzing 0.9.9b)
breadboards: 1

parts:
  DRV_2 = DRV 8825 Stepper Motor Carrier, High Current [part_number="DRV 8825"]
  Mod1 = Raspberry Pi 4B
  U2 = LIPO-110mAh [package=lipo-110]
  C2 = Capacitor Polarized [package=panasonic_c]
  DRV_1 = DRV 8825 Stepper Motor Carrier, High Current [part_number="DRV 8825"]
  M1 = RioRand LM2596
  M2 = Stepper Motor - Bipolar
  M3 = Stepper Motor - Bipolar

nets:
  N1: DRV_2.RESET, DRV_2.SLEEP, Mod1.5V, M1.Pin_3
  N2: DRV_2.STEP, Mod1.GPIO8
  N3: DRV_2.DIRECTION, Mod1.GPIO25
  N4: DRV_2.VOLTAGE_ST/_MT, U2.+, C2.+, DRV_1.VOLTAGE_ST/_MT, M1.Pin_1
  N5: DRV_2.GROUND_ST/_MT, U2.-, C2.-, DRV_1.GROUND_ST/_MT, M1.Pin_2
  N6: DRV_2.OUT_2B, M3.A
  N7: DRV_2.OUT_2A, M3.C
  N8: DRV_2.OUT_1A, M3.B
  N9: DRV_2.OUT_1B, M3.D
  N10: Mod1.GND, M1.Pin_4
  N11: Mod1.GPIO7, DRV_1.DIRECTION
  N12: Mod1.ID_SC, DRV_1.STEP
  N13: DRV_1.OUT_2B, M2.D
  N14: DRV_1.OUT_2A, M2.B
  N15: DRV_1.OUT_1A, M2.A
  N16: DRV_1.OUT_1B, M2.C
